// Logisim project CPU_3.circ as structural Verilog: 10 circuits, main circuit main
module main (
  output [31:0] out_1,
  output out_2
);

  wire ALUSrc, clk, control_1_branch, control_1_jump, control_1_memread, control_1_memtoreg,
       control_1_memwrite, control_1_regwrite, RegDst, Reset, undriven, undriven_2;
  wire [1:0] ALUOp;
  wire [3:0] alu_control_1_out_3;
  wire [4:0] id_1_rd, id_1_rs, id_1_rt, id_1_sh, multiplexer_1_out;
  wire [5:0] \function , opcode;
  wire [7:0] rd_display, rs_display, rt_display;
  wire [15:0] id_1_off, immediate_display;
  wire [20:0] instruccion_display;
  wire [23:0] bit_extender_1_out;
  wire [25:0] id_1_add;
  wire [31:0] adder_1_out, bit_extender_2_out, inst, multiplexer_2_out, PC_q, register_memory_1_busa,
       register_memory_1_busb;

  Clock clock_1 (.out(clk));
  Button u_Reset (.out(Reset));
  Register #(.width(32)) PC (.D(adder_1_out), .Q(PC_q), .clk(clk), .clr(Reset));  // open: en
  debug debug_1 (
    .instruccion(inst), .display_instruccion(instruccion_display), .rs(rs_display), .rt(rt_display),
    .rd(rd_display), .immediate(immediate_display));
  Bit_Extender #(.in_width(32), .out_width(24)) bit_extender_1 (.in(PC_q), .out(bit_extender_1_out));
  _7_Segment_Display u_7_segment_display_1 (
    .g(instruccion_display[20]), .f(instruccion_display[19]), .a(instruccion_display[18]),
    .b(instruccion_display[17]), .e(instruccion_display[16]), .d(instruccion_display[15]),
    .c(instruccion_display[14]));  // open: dp
  Adder #(.width(32)) adder_1 (.a(PC_q), .b(32'h1), .out(adder_1_out));  // open: cin, cout
  RAM #(.addrWidth(24), .dataWidth(32)) ram_1 (
    .addr(bit_extender_1_out), .data(inst), .clk(clk));  // open: sel, ld, clr
  _7_Segment_Display u_7_segment_display_2 (
    .g(instruccion_display[6]), .f(instruccion_display[5]), .a(instruccion_display[4]),
    .b(instruccion_display[3]), .e(instruccion_display[2]), .d(instruccion_display[1]),
    .c(instruccion_display[0]));  // open: dp
  _7_Segment_Display u_7_segment_display_3 (
    .g(instruccion_display[13]), .f(instruccion_display[12]), .a(instruccion_display[11]),
    .b(instruccion_display[10]), .e(instruccion_display[9]), .d(instruccion_display[8]),
    .c(instruccion_display[7]));  // open: dp
  ID id_1 (
    .Input(inst), .op(opcode), .rs(id_1_rs), .rt(id_1_rt), .rd(id_1_rd), .sh(id_1_sh), .func(\function ),
    .off(id_1_off), .add(id_1_add));
  // Probe on id_1_sh
  // Probe on id_1_off
  // Probe on id_1_add
  Hex_Digit_Display hex_digit_display_1 (.value(rs_display[7:4]));  // open: dp
  Hex_Digit_Display hex_digit_display_2 (.value(rs_display[3:0]));  // open: dp
  Hex_Digit_Display hex_digit_display_3 (.value(rt_display[7:4]));  // open: dp
  Hex_Digit_Display hex_digit_display_4 (.value(rt_display[3:0]));  // open: dp
  Hex_Digit_Display hex_digit_display_5 (.value(rd_display[7:4]));  // open: dp
  Control control_1 (
    .opcode(opcode), .RegDst(RegDst), .ALUSrc(ALUSrc), .MemtoReg(control_1_memtoreg),
    .RegWrite(control_1_regwrite), .MemRead(control_1_memread), .MemWrite(control_1_memwrite),
    .Branch(control_1_branch), .Jump(control_1_jump), .ALUOp(ALUOp));
  Hex_Digit_Display hex_digit_display_6 (.value(rd_display[3:0]));  // open: dp
  Multiplexer #(.width(5)) multiplexer_1 (
    .in0(id_1_rt), .in1(id_1_rd), .out(multiplexer_1_out), .sel(undriven), .en(RegDst));
  Register_Memory register_memory_1 (
    .reset(Reset), .clk(clk), .busA(register_memory_1_busa), .busB(register_memory_1_busb), .RA(id_1_rs),
    .RW(multiplexer_1_out), .RB(id_1_rt));  // open: WriteEnable, busW
  ALU_control alu_control_1 (.ALUOp(ALUOp), .\function (\function ), .out_3(alu_control_1_out_3));
  Hex_Digit_Display hex_digit_display_7 (.value(immediate_display[11:8]));  // open: dp
  Hex_Digit_Display hex_digit_display_8 (.value(immediate_display[15:12]));  // open: dp
  // Probe on control_1_memtoreg
  // Probe on control_1_regwrite
  // Probe on control_1_memread
  // Probe on control_1_memwrite
  // Probe on control_1_branch
  // Probe on control_1_jump
  assign bit_extender_2_out = {{16{1'b0}}, inst[15:0]};  // Bit_Extender bit_extender_2
  Hex_Digit_Display hex_digit_display_9 (.value(immediate_display[3:0]));  // open: dp
  Hex_Digit_Display hex_digit_display_10 (.value(immediate_display[7:4]));  // open: dp
  Multiplexer #(.width(32)) multiplexer_2 (
    .in0(register_memory_1_busb), .in1(bit_extender_2_out), .out(multiplexer_2_out), .sel(undriven_2),
    .en(ALUSrc));
  ALU alu_1 (.Opcode(alu_control_1_out_3), .A(register_memory_1_busa), .B(multiplexer_2_out), .Y(out_1), .Cout(out_2));
  // Probe on alu_control_1_out_3

  // Notes on the sheet:
  //   RS
  //   RT
  //   RD
  //   IMMEDIATE
endmodule

module ID (
  input  [31:0] Input,
  output [25:0] add,
  output [15:0] off,
  output [5:0] func,
  output [4:0] sh,
  output [4:0] rd,
  output [4:0] rt,
  output [4:0] rs,
  output [5:0] op
);


  assign add = Input[25:0];
  assign func = Input[5:0];
  assign off = Input[15:0];
  assign op = Input[31:26];
  assign rd = Input[15:11];
  assign rs = Input[25:21];
  assign rt = Input[20:16];
  assign sh = Input[10:6];
endmodule

module Control (
  input  [5:0] opcode,
  output RegDst,
  output ALUSrc,
  output MemtoReg,
  output RegWrite,
  output MemRead,
  output MemWrite,
  output Branch,
  output [1:0] ALUOp,
  output Jump
);

  wire and_2_out, and_3_out, and_4_out, and_5_out, and_6_out, and_7_out, and_8_out, and_9_out, and_10_out,
       and_11_out, and_12_out, and_13_out, and_14_out, and_15_out, and_16_out, and_17_out, and_18_out,
       and_19_out, and_20_out, and_21_out, and_23_out, and_24_out, and_25_out, not_1_out, not_2_out,
       not_3_out, not_4_out, not_5_out, not_6_out, not_7_out, not_8_out, not_9_out, not_10_out, not_11_out,
       not_12_out, not_13_out, not_14_out, not_15_out, not_16_out, not_17_out, not_18_out, not_19_out,
       not_20_out, not_21_out, not_22_out, not_23_out, not_24_out, not_25_out, not_26_out, not_27_out,
       not_28_out, not_29_out;

  not not_1 (not_1_out, opcode[3]);
  not not_2 (not_2_out, opcode[1]);
  not not_3 (not_3_out, opcode[2]);
  not not_4 (not_4_out, opcode[1]);
  not not_5 (not_5_out, opcode[3]);
  not not_6 (not_6_out, opcode[2]);
  not not_7 (not_7_out, opcode[3]);
  not not_8 (not_8_out, opcode[2]);
  not not_9 (not_9_out, opcode[3]);
  not not_10 (not_10_out, opcode[2]);
  not not_11 (not_11_out, opcode[3]);
  not not_12 (not_12_out, opcode[3]);
  not not_13 (not_13_out, opcode[1]);
  not not_14 (not_14_out, opcode[1]);
  not not_15 (not_15_out, opcode[3]);
  not not_16 (not_16_out, opcode[1]);
  not not_17 (not_17_out, opcode[3]);
  not not_18 (not_18_out, opcode[1]);
  not not_19 (not_19_out, opcode[0]);
  not not_20 (not_20_out, opcode[0]);
  not not_21 (not_21_out, opcode[0]);
  not not_22 (not_22_out, opcode[3]);
  not not_23 (not_23_out, opcode[2]);
  not not_24 (not_24_out, opcode[1]);
  not not_25 (not_25_out, opcode[5]);
  not not_26 (not_26_out, opcode[4]);
  not not_27 (not_27_out, opcode[3]);
  not not_28 (not_28_out, opcode[2]);
  not not_29 (not_29_out, opcode[0]);
  and and_1 (RegDst, not_1_out, not_2_out);
  and and_2 (and_2_out, opcode[1], opcode[0]);
  and and_3 (and_3_out, opcode[2], opcode[1]);
  and and_4 (and_4_out, opcode[4], opcode[1]);
  and and_5 (and_5_out, opcode[5], opcode[1]);
  and and_6 (and_6_out, opcode[1], opcode[0]);
  and and_7 (and_7_out, opcode[2], opcode[1]);
  and and_8 (and_8_out, opcode[4], opcode[1]);
  and and_9 (and_9_out, opcode[5], opcode[1]);
  and and_10 (and_10_out, not_3_out, not_4_out);
  and and_11 (and_11_out, not_5_out, not_6_out, opcode[0]);
  and and_12 (and_12_out, opcode[4], not_7_out, not_8_out);
  and and_13 (and_13_out, opcode[5], not_9_out, not_10_out);
  and and_14 (and_14_out, not_11_out, opcode[1], opcode[0]);
  and and_15 (and_15_out, not_12_out, opcode[2], opcode[1]);
  and and_16 (and_16_out, opcode[3], not_13_out, opcode[0]);
  and and_17 (and_17_out, opcode[3], opcode[2], not_14_out);
  and and_18 (and_18_out, opcode[4], not_15_out, opcode[1]);
  and and_19 (and_19_out, opcode[4], opcode[3], not_16_out);
  and and_20 (and_20_out, opcode[5], not_17_out, opcode[1]);
  and and_21 (and_21_out, opcode[5], opcode[3], not_18_out);
  and and_22 (MemWrite, opcode[5], opcode[3]);
  and and_23 (and_23_out, opcode[3], opcode[1], not_19_out);
  and and_24 (and_24_out, opcode[4], opcode[1], not_20_out);
  and and_25 (and_25_out, opcode[5], opcode[1], not_21_out);
  and and_26 (ALUOp[1], not_22_out, not_23_out, not_24_out);
  or or_1 (ALUSrc, and_2_out, and_3_out, opcode[3], and_4_out, and_5_out);
  or or_2 (MemtoReg, and_6_out, and_7_out, opcode[3], and_8_out, and_9_out);
  or or_3 (RegWrite, and_10_out, and_11_out, and_12_out, and_13_out);
  or or_4 (Branch, opcode[2], and_23_out, and_24_out, and_25_out);
  and and_27 (Jump, not_25_out, not_26_out, not_27_out, not_28_out, opcode[1], not_29_out);
  or or_5 (MemRead, and_14_out, and_15_out, and_16_out, and_17_out, and_18_out, and_19_out, and_20_out, and_21_out);

  assign ALUOp[0] = opcode[2];
endmodule

module debug (
  input  [31:0] instruccion,
  output [20:0] display_instruccion,
  output [7:0] rs,
  output [7:0] rt,
  output [7:0] rd,
  output [15:0] immediate
);

  wire and_2_out, and_3_out, and_4_out, comparator_1_eq, not_1_out, not_2_out, not_3_out, not_4_out,
       not_5_out;
  wire [0:0] or_1_out;
  wire [2:0] or_3_out;
  wire [4:0] id_1_rd, id_1_rs, id_1_rt;
  wire [5:0] id_1_func, id_1_op;
  wire [7:0] bit_extender_1_out;
  wire [15:0] id_1_off;
  wire [20:0] multiplexer_3_out, multiplexer_4_out;

  ID id_1 (
    .Input(instruccion), .op(id_1_op), .rs(id_1_rs), .rt(id_1_rt), .rd(id_1_rd), .func(id_1_func),
    .off(id_1_off));  // open: sh, add
  or or_1 (or_1_out[0], id_1_func[0], id_1_func[1]);
  Comparator #(.width(6)) comparator_1 (.a({6{1'b0}}), .b(id_1_op), .eq(comparator_1_eq));  // open: gt, lt
  Multiplexer #(.width(8), .disabled(0)) multiplexer_1 (
    .in1(bit_extender_1_out), .out(rd), .sel(comparator_1_eq));  // open: in0, en
  assign bit_extender_1_out = {{3{1'b0}}, id_1_rd};  // Bit_Extender bit_extender_1
  Multiplexer #(.width(16), .disabled(0)) multiplexer_2 (
    .in0(id_1_off), .out(immediate), .sel(comparator_1_eq));  // open: in1, en
  assign rs = {{3{1'b0}}, id_1_rs};  // Bit_Extender bit_extender_2
  assign rt = {{3{1'b0}}, id_1_rt};  // Bit_Extender bit_extender_3
  and and_1 (or_3_out[2], id_1_op[5], id_1_op[3]);
  not not_1 (not_1_out, id_1_op[2]);
  and and_2 (and_2_out, not_1_out, not_2_out);
  not not_2 (not_2_out, id_1_op[1]);
  and and_3 (and_3_out, id_1_op[5], not_3_out);
  not not_3 (not_3_out, id_1_op[3]);
  and and_4 (and_4_out, id_1_op[5], not_4_out);
  not not_4 (not_4_out, id_1_op[3]);
  or or_2 (or_3_out[1], and_2_out, and_3_out);
  or or_3 (or_3_out[0], id_1_op[2], and_4_out);
  Multiplexer #(.select(2), .width(21), .disabled(0)) multiplexer_3 (
    .in0(21'h1f67cf), .in1(21'h1cd7e7), .in2(21'h1f5ecf), .in3(21'h1fc4), .out(multiplexer_3_out),
    .sel({id_1_func[2], or_1_out[0]}));  // open: en
  Multiplexer #(.select(3), .width(21), .disabled(0)) multiplexer_4 (
    .in0(21'hb), .in1(21'h19fb79), .in2(21'h1f6789), .in3(21'h99ffd), .in4(21'h1cf33f),
    .out(multiplexer_4_out), .sel(or_3_out));  // open: in5, in6, in7, en
  Multiplexer #(.width(21), .disabled(0)) multiplexer_5 (
    .in0(multiplexer_3_out), .in1(multiplexer_4_out), .out(display_instruccion), .sel(not_5_out));  // open: en
  not not_5 (not_5_out, comparator_1_eq);
  // Probe on display_instruccion

  // Notes on the sheet:
  //   Enumera los functions de las tipo R
  //   Es tipo R?
  //   Codificación de los 3 displays de 7 segmentos
  //   add
  //   sub
  //   and
  //   or
  //   Enumera los opcodes de las instrucciones tipo I y J
  //   jump
  //   beq
  //   addi
  //   lw
  //   sw
endmodule

// ALU_CONTROL
module ALU_control (
  input  [1:0] ALUOp,
  input  [5:0] \function ,
  output [3:0] out_3
);

  wire and_1_out, and_2_out, and_3_out, and_4_out, not_1_out, not_2_out, not_3_out;

  // Probe on \function [5]
  // Probe on \function [4]
  not not_1 (not_1_out, ALUOp[1]);
  and and_1 (and_1_out, not_1_out, ALUOp[0]);
  and and_2 (and_2_out, ALUOp[1], \function [1]);
  not not_2 (not_2_out, ALUOp[1]);
  or or_1 (out_3[1], not_2_out, not_3_out);
  not not_3 (not_3_out, \function [2]);
  and and_3 (and_3_out, ALUOp[1], \function [0]);
  or or_2 (out_3[0], and_3_out, and_4_out);
  and and_4 (and_4_out, ALUOp[1], \function [3]);
  or or_3 (out_3[2], and_1_out, and_2_out);

  assign out_3[3] = 1'b0;
endmodule

module Register_Memory (
  input  clk,
  input  WriteEnable,
  input  reset,
  input  [31:0] busW,
  input  [4:0] RW,
  input  [4:0] RA,
  input  [4:0] RB,
  output [31:0] busA,
  output [31:0] busB
);

  wire and_1_out, clk0, clk1, clk2, clk3, clk4, clk5, clk6, clk7, clk8, clk9, clk10, clk11, clk12, clk13,
       clk14, clk15, clk16, clk17, clk18, clk19, clk20, clk21, clk22, clk23, clk24, clk25, clk26, clk27,
       clk28, clk29, clk30, clk31;
  wire [31:0] bus0, bus1, bus2, bus3, bus4, bus5, bus6, bus7, bus8, bus9, bus10, bus11, bus12, bus13, bus14,
       bus15, bus16, bus17, bus18, bus19, bus20, bus21, bus22, bus23, bus24, bus25, bus26, bus27, bus28,
       bus29, bus30, bus31;

  Register #(.width(32)) zero (.D(busW), .Q(bus0), .clk(clk0), .clr(reset));  // open: en
  Register #(.width(32)) at (.D(busW), .Q(bus1), .clk(clk1), .clr(reset));  // open: en
  Register #(.width(32)) v0 (.D(busW), .Q(bus2), .clk(clk2), .clr(reset));  // open: en
  Register #(.width(32)) v1 (.D(busW), .Q(bus3), .clk(clk3), .clr(reset));  // open: en
  Register #(.width(32)) a0 (.D(busW), .Q(bus4), .clk(clk4), .clr(reset));  // open: en
  Register #(.width(32)) a1 (.D(busW), .Q(bus5), .clk(clk5), .clr(reset));  // open: en
  Register #(.width(32)) a2 (.D(busW), .Q(bus6), .clk(clk6), .clr(reset));  // open: en
  Register #(.width(32)) a3 (.D(busW), .Q(bus7), .clk(clk7), .clr(reset));  // open: en
  Register #(.width(32)) t0 (.D(busW), .Q(bus8), .clk(clk8), .clr(reset));  // open: en
  Register #(.width(32)) t1 (.D(busW), .Q(bus9), .clk(clk9), .clr(reset));  // open: en
  Register #(.width(32)) t2 (.D(busW), .Q(bus10), .clk(clk10), .clr(reset));  // open: en
  Register #(.width(32)) t3 (.D(busW), .Q(bus11), .clk(clk11), .clr(reset));  // open: en
  Register #(.width(32)) t4 (.D(busW), .Q(bus12), .clk(clk12), .clr(reset));  // open: en
  Register #(.width(32)) t5 (.D(busW), .Q(bus13), .clk(clk13), .clr(reset));  // open: en
  Register #(.width(32)) t6 (.D(busW), .Q(bus14), .clk(clk14), .clr(reset));  // open: en
  Register #(.width(32)) t7 (.D(busW), .Q(bus15), .clk(clk15), .clr(reset));  // open: en
  Register #(.width(32)) s0 (.D(busW), .Q(bus16), .clk(clk16), .clr(reset));  // open: en
  Register #(.width(32)) s1 (.D(busW), .Q(bus17), .clk(clk17), .clr(reset));  // open: en
  Register #(.width(32)) s2 (.D(busW), .Q(bus18), .clk(clk18), .clr(reset));  // open: en
  Register #(.width(32)) s3 (.D(busW), .Q(bus19), .clk(clk19), .clr(reset));  // open: en
  Register #(.width(32)) s4 (.D(busW), .Q(bus20), .clk(clk20), .clr(reset));  // open: en
  Register #(.width(32)) s5 (.D(busW), .Q(bus21), .clk(clk21), .clr(reset));  // open: en
  Register #(.width(32)) s6 (.D(busW), .Q(bus22), .clk(clk22), .clr(reset));  // open: en
  Register #(.width(32)) s7 (.D(busW), .Q(bus23), .clk(clk23), .clr(reset));  // open: en
  Register #(.width(32)) t8 (.D(busW), .Q(bus24), .clk(clk24), .clr(reset));  // open: en
  Register #(.width(32)) t9 (.D(busW), .Q(bus25), .clk(clk25), .clr(reset));  // open: en
  Register #(.width(32)) k0 (.D(busW), .Q(bus26), .clk(clk26), .clr(reset));  // open: en
  Register #(.width(32)) k1 (.D(busW), .Q(bus27), .clk(clk27), .clr(reset));  // open: en
  Register #(.width(32)) gp (.D(busW), .Q(bus28), .clk(clk28), .clr(reset));  // open: en
  Register #(.width(32)) sp (.D(busW), .Q(bus29), .clk(clk29), .clr(reset));  // open: en
  Register #(.width(32)) fp (.D(busW), .Q(bus30), .clk(clk30), .clr(reset));  // open: en
  Register #(.width(32)) u_ra (.D(busW), .Q(bus31), .clk(clk31), .clr(reset));  // open: en
  and and_1 (and_1_out, clk, WriteEnable);
  Demultiplexer #(.select(5)) demultiplexer_1 (
    .out0(clk0), .out1(clk1), .out2(clk2), .out3(clk3), .out4(clk4), .out5(clk5), .out6(clk6), .out7(clk7),
    .out8(clk8), .out9(clk9), .out10(clk10), .out11(clk11), .out12(clk12), .out13(clk13), .out14(clk14),
    .out15(clk15), .out16(clk16), .out17(clk17), .out18(clk18), .out19(clk19), .out20(clk20), .out21(clk21),
    .out22(clk22), .out23(clk23), .out24(clk24), .out25(clk25), .out26(clk26), .out27(clk27), .out28(clk28),
    .out29(clk29), .out30(clk30), .out31(clk31), .in(and_1_out), .sel(RW));  // open: en
  Multiplexer #(.select(5), .width(32)) multiplexer_1 (
    .in0(bus0), .in1(bus1), .in2(bus2), .in3(bus3), .in4(bus4), .in5(bus5), .in6(bus6), .in7(bus7),
    .in8(bus8), .in9(bus9), .in10(bus10), .in11(bus11), .in12(bus12), .in13(bus13), .in14(bus14),
    .in15(bus15), .in16(bus16), .in17(bus17), .in18(bus18), .in19(bus19), .in20(bus20), .in21(bus21),
    .in22(bus22), .in23(bus23), .in24(bus24), .in25(bus25), .in26(bus26), .in27(bus27), .in28(bus28),
    .in29(bus29), .in30(bus30), .in31(bus31), .out(busA), .sel(RA));  // open: en
  Multiplexer #(.select(5), .width(32)) multiplexer_2 (
    .in0(bus0), .in1(bus1), .in2(bus2), .in3(bus3), .in4(bus4), .in5(bus5), .in6(bus6), .in7(bus7),
    .in8(bus8), .in9(bus9), .in10(bus10), .in11(bus11), .in12(bus12), .in13(bus13), .in14(bus14),
    .in15(bus15), .in16(bus16), .in17(bus17), .in18(bus18), .in19(bus19), .in20(bus20), .in21(bus21),
    .in22(bus22), .in23(bus23), .in24(bus24), .in25(bus25), .in26(bus26), .in27(bus27), .in28(bus28),
    .in29(bus29), .in30(bus30), .in31(bus31), .out(busB), .sel(RB));  // open: en
endmodule

module ALU (
  input  [3:0] Opcode,
  input  [31:0] A,
  input  [31:0] B,
  output [31:0] Y,
  output Cout
);

  wire [31:0] lu_32bits_1_y, multiplexer_1_out, multiplexer_2_out, not_1_out, not_2_out, undriven;

  assign not_1_out = ~A;  // NOT_Gate not_1, 32 bits wide
  assign not_2_out = ~B;  // NOT_Gate not_2, 32 bits wide
  Multiplexer #(.width(32), .enable("false")) multiplexer_1 (
    .in0(A), .in1(not_1_out), .out(multiplexer_1_out), .sel(Opcode[0]));
  Multiplexer #(.width(32), .enable("false")) multiplexer_2 (
    .in0(B), .in1(not_2_out), .out(multiplexer_2_out), .sel(Opcode[1]));
  AU_32bits au_32bits_1 (.Cin(Opcode[2]), .Cout(Cout), .A(multiplexer_1_out), .B(multiplexer_2_out), .s(undriven));
  LU_32bits lu_32bits_1 (.A(A), .B(multiplexer_2_out), .Y(lu_32bits_1_y), .f2(Opcode[2]), .f0(Opcode[0]));
  Multiplexer #(.width(32), .enable("false")) multiplexer_3 (
    .in0(undriven), .in1(lu_32bits_1_y), .out(Y), .sel(Opcode[3]));

  // Other names for the same wires on the sheet: f0 = Opcode[0]; f1 = Opcode[1]; f2 = Opcode[2]; f3 = Opcode[3]
endmodule

module AU_4bits (
  input  Cin,
  input  [3:0] A,
  input  [3:0] B,
  output Cout,
  output [3:0] B_2
);

  wire adder_1_cout, adder_2_cout, adder_3_cout;

  Adder #(.width(1)) adder_1 (.a(B[0]), .b(A[0]), .out(B_2[0]), .cin(Cin), .cout(adder_1_cout));
  Adder #(.width(1)) adder_2 (.a(B[1]), .b(A[1]), .out(B_2[1]), .cin(adder_1_cout), .cout(adder_2_cout));
  Adder #(.width(1)) adder_3 (.a(B[2]), .b(A[2]), .out(B_2[2]), .cin(adder_2_cout), .cout(adder_3_cout));
  Adder #(.width(1)) adder_4 (.a(B[3]), .b(A[3]), .out(B_2[3]), .cin(adder_3_cout), .cout(Cout));
endmodule

module LU_32bits (
  input  [31:0] A,
  input  [31:0] B,
  input  f2,
  input  f0,
  output [31:0] Y
);

  wire [31:0] and_1_out, or_1_out, xor_1_out;

  assign and_1_out = A & B;  // AND_Gate and_1, 32 bits wide
  assign or_1_out = A | B;  // OR_Gate or_1, 32 bits wide
  assign xor_1_out = A ^ B;  // XOR_Gate xor_1, 32 bits wide
  Multiplexer #(.select(2), .width(32), .enable("false")) multiplexer_1 (
    .in0(and_1_out), .in1(or_1_out), .in2(xor_1_out), .in3(B), .out(Y), .sel({f2, f0}));
endmodule

module AU_32bits (
  input  Cin,
  input  [31:0] A,
  input  [31:0] s,
  input  [31:0] B,
  output Cout
);

  wire au_4bits_1_cout, au_4bits_2_cout, au_4bits_3_cout, au_4bits_4_cout, au_4bits_5_cout, au_4bits_6_cout,
       au_4bits_7_cout;

  AU_4bits au_4bits_1 (.Cin(Cin), .Cout(au_4bits_1_cout), .A(A[3:0]), .B(B[3:0]), .B_2(s[3:0]));
  AU_4bits au_4bits_2 (.Cin(au_4bits_1_cout), .Cout(au_4bits_2_cout), .A(A[7:4]), .B(B[7:4]), .B_2(s[7:4]));
  AU_4bits au_4bits_3 (.Cin(au_4bits_2_cout), .Cout(au_4bits_3_cout), .A(A[11:8]), .B(B[11:8]), .B_2(s[11:8]));
  AU_4bits au_4bits_4 (.Cin(au_4bits_3_cout), .Cout(au_4bits_4_cout), .A(A[15:12]), .B(B[15:12]), .B_2(s[15:12]));
  AU_4bits au_4bits_5 (.Cin(au_4bits_4_cout), .Cout(au_4bits_5_cout), .A(A[19:16]), .B(B[19:16]), .B_2(s[19:16]));
  AU_4bits au_4bits_6 (.Cin(au_4bits_5_cout), .Cout(au_4bits_6_cout), .A(A[23:20]), .B(B[23:20]), .B_2(s[23:20]));
  AU_4bits au_4bits_7 (.Cin(au_4bits_6_cout), .Cout(au_4bits_7_cout), .A(A[27:24]), .B(B[27:24]), .B_2(s[27:24]));
  AU_4bits au_4bits_8 (.Cin(au_4bits_7_cout), .Cout(Cout), .A(A[31:28]), .B(B[31:28]), .B_2(s[31:28]));

  // Other names for the same wires on the sheet: A_1_4[3:0] = A[3:0]; A_5_8[3:0] = A[7:4]; A_9_12[3:0] = A[11:8];
  //   A_13_16[3:0] = A[15:12]; A_17_20[3:0] = A[19:16]; A_21_24[3:0] = A[23:20]; A_25_28[3:0] = A[27:24];
  //   A_29_32[3:0] = A[31:28]; B_1_4[3:0] = B[3:0]; B_5_8[3:0] = B[7:4]; B_9_12[3:0] = B[11:8];
  //   B_13_16[3:0] = B[15:12]; B_17_20[3:0] = B[19:16]; B_21_24[3:0] = B[23:20]; B_25_28[3:0] = B[27:24];
  //   B_29_32[3:0] = B[31:28]; s1_4[3:0] = s[3:0]; s5_8[3:0] = s[7:4]; s9_12[3:0] = s[11:8]; s13_16[3:0] = s[15:12];
  //   s17_20[3:0] = s[19:16]; s21_24[3:0] = s[23:20]; s25_28[3:0] = s[27:24]; s29_32[3:0] = s[31:28]

  // Notes on the sheet:
  //   INPUT
  //   OUPUT
endmodule
